# Fritzing sketch Silicon_Limitter (saved by Fritzing 0.9.3b)
breadboards: 1

parts:
  R1 = Resistor [tolerance=±5% resistance=1k package=THT]  # not connected
  D1 = Rectifier Diode [part_number=1N4001 package="300 mil [THT]"]  # not connected
  D2 = Rectifier Diode [part_number=1N4001 package="300 mil [THT]"]  # not connected
  R2 = TRIMPOT [package=trimpot_pth_s3_lock]
  VCC1 = Battery

nets:
  N1: R2.CCW, VCC1.+
  N2: R2.CW, VCC1.-

notes:
  IN
  OUT
  1N4148
  GND
  +1V
  100Ω Trim
