# Fritzing sketch Zenerx2_Limitter (saved by Fritzing 0.9.3b)
breadboards: 1

parts:
  R1 = Resistor [tolerance=±5% resistance=1k package=THT]
  D1 = Rectifier Diode [part_number=1N4001 package="300 mil [THT]"]
  D2 = Rectifier Diode [part_number=1N4001 package="300 mil [THT]"]

nets:
  N1: R1.Pin_1, D1.cathode
  N2: D1.anode, D2.anode

notes:
  IN
  OUT
  1.8V Zener
